// Logisim project misc16bit.circ as structural Verilog: 2 circuits, main circuit main
module main (
  input  in_1
);

  wire and_1_out, button_1_out, data_flag, data_instr_out, demultiplexer_1_out5, execute, fetch, inc_IAR,
       multiplexer_2_out, write;
  wire [2:0] counter_1_q;
  wire [15:0] adder_1_out, D_q, demultiplexer_2_out0, demultiplexer_2_out1, IAR_q, IR_q, JAR_q, KR_q, MAR_q,
       multiplexer_1_out, pull_resistor_1_node, R0_q, R1_q, R2_q, ram_1_dout, rom_1_data;

  Pull_Resistor pull_resistor_1 (.node(pull_resistor_1_node));
  Register #(.width(16)) MAR (.D(pull_resistor_1_node), .Q(MAR_q));  // open: en, clk, clr
  // Probe on pull_resistor_1_node
  Counter #(.max('h7), .width(3)) counter_1 (
    .Q(counter_1_q), .clk(button_1_out), .clr(demultiplexer_1_out5));  // open: load, D, count, carry, up
  Button button_1 (.out(button_1_out));
  ROM #(.addrWidth(16), .dataWidth(16)) rom_1 (.addr(IAR_q), .data(rom_1_data));
  RAM #(.addrWidth(16), .dataWidth(16), .trigger("high")) ram_1 (.addr(MAR_q), .dout(ram_1_dout));  // open: we, oe, din
  Controlled_Buffer #(.width(16)) controlled_buffer_1 (.in(MAR_q), .out(pull_resistor_1_node));  // open: en
  Demultiplexer #(.select(3)) demultiplexer_1 (
    .out1(fetch), .out2(execute), .out3(write), .out4(inc_IAR), .out5(demultiplexer_1_out5), .in(1'b1),
    .sel(counter_1_q));  // open: out0, out6, out7
  Adder #(.width(16)) adder_1 (.a(16'h1), .b(IAR_q), .out(adder_1_out));  // open: cin, cout
  Multiplexer #(.width(16)) multiplexer_1 (.in0(adder_1_out), .in1(JAR_q), .out(multiplexer_1_out), .sel(in_1));
  Register #(.width(16)) IAR (.D(multiplexer_1_out), .clk(inc_IAR), .Q(IAR_q));  // open: en, clr
  Controlled_Buffer #(.width(16)) controlled_buffer_2 (.in(IAR_q), .out(pull_resistor_1_node));  // open: en
  Demultiplexer #(.width(16)) demultiplexer_2 (
    .out0(demultiplexer_2_out0), .out1(demultiplexer_2_out1), .in(rom_1_data), .sel(data_flag));
  Register #(.width(16)) D (.D(demultiplexer_2_out1), .clk(and_1_out), .Q(D_q));  // open: en, clr
  Controlled_Buffer #(.width(16)) controlled_buffer_3 (.in(D_q), .out(pull_resistor_1_node));  // open: en
  and and_1 (and_1_out, fetch, data_flag);
  Register #(.width(16)) R0 (.D(pull_resistor_1_node), .Q(R0_q));  // open: en, clk, clr
  Controlled_Buffer #(.width(16)) controlled_buffer_4 (.in(R0_q), .out(pull_resistor_1_node));  // open: en
  Register #(.width(16)) IR (.D(demultiplexer_2_out0), .clk(fetch), .Q(IR_q));  // open: en, clr
  Register #(.width(16)) R1 (.D(pull_resistor_1_node), .Q(R1_q));  // open: en, clk, clr
  control_unit control_unit_1 (.in_1(IR_q));
  Controlled_Buffer #(.width(16)) controlled_buffer_5 (.in(R1_q), .out(pull_resistor_1_node));  // open: en
  Register #(.width(16)) R2 (.D(pull_resistor_1_node), .Q(R2_q));  // open: en, clk, clr
  Controlled_Buffer #(.width(16)) controlled_buffer_6 (.in(R2_q), .out(pull_resistor_1_node));  // open: en
  and data_instr (data_instr_out, IR_q[12], ~IR_q[13], ~IR_q[14], ~IR_q[15]);  // AND_Gate
  Register #(.width(16)) JAR (.D(pull_resistor_1_node), .Q(JAR_q));  // open: en, clk, clr
  Multiplexer multiplexer_2 (.in0(data_instr_out), .in1(1'b0), .out(multiplexer_2_out), .sel(data_flag));
  D_Flip_Flop d_ff_1 (.D(multiplexer_2_out), .clk(execute), .Q(data_flag));  // open: Qn, preset, reset
  Register #(.width(16)) KR (.D(pull_resistor_1_node), .Q(KR_q));  // open: en, clk, clr
  Controlled_Buffer #(.width(16)) controlled_buffer_7 (.in(KR_q), .out(pull_resistor_1_node));  // open: en
  Controlled_Buffer #(.width(16)) controlled_buffer_8 (.in(ram_1_dout), .out(pull_resistor_1_node));  // open: en

  // Notes on the sheet:
  //   contents of rom_1 (hex, n*v repeats v):
  //   1000 5
endmodule

module control_unit (
  input  [15:0] in_1
);
endmodule
